# Fritzing sketch Schéma Drone (saved by Fritzing 0.9.3b)
breadboards: 1

parts:
  Composant1 = Adafruit HUZZAH32 ESP32 Feather [part_number="Adafruit #3405"]  # not connected
  NRF24L1 = NRF24L01
  Composant2 = Adafruit DC+Stepper FeatherWing [part_number="Adafruit #2927"]
  M1 = DC Motor
  M2 = DC Motor
  M3 = DC Motor
  M4 = DC Motor
  Composant3 = LSM9DS0 9DOF Accel/Mag/Gyro+Temp
  U1 = LIPO-1000mAh [package=lipo-1000]

nets:
  VCC: NRF24L1.VCC, Composant2.+3.3V, Composant3.VIN
  N1: NRF24L1.CSN, Composant2.I
  N2: NRF24L1.MOSI, Composant2.MOSI
  GND: NRF24L1.GND, Composant2.GND, Composant3.GND, U1.-
  N3: NRF24L1.CE, Composant2.H
  N4: NRF24L1.SCK, Composant2.SCK
  N5: NRF24L1.MISO, Composant2.MISO
  N6: Composant2.SCL, Composant3.SCL_5V
  N7: Composant2.SDA, Composant3.SDA_5V
  N8: Composant2.VMOTOR, U1.+
  N9: Composant2.M1B, M2.pin_1
  N10: Composant2.M1A, M2.pin_2
  N11: Composant2.M2A, M4.pin_1
  N12: Composant2.M2B, M4.pin_2
  N13: Composant2.M3B, M1.pin_1
  N14: Composant2.M3A, M1.pin_2
  N15: Composant2.M4A, M3.pin_1
  N16: Composant2.M4B, M3.pin_2

custom parts:
  NRF24L01: NRF24L01 module
  Adafruit DC+Stepper FeatherWing: This is the DC Motor + Stepper FeatherWing which will let you use 2 x bi-polar stepper motors or 4 x brushed DC motorx (or 1 stepper and 2 DC motors). Using our Feather Stacking Headers or Feather Female Headers you can connect a FeatherWing on top or bottom of your Feather board and let the board take flight! The original Adafruit Motorshield Kit is one of our most beloved kits, which is why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
  LSM9DS0 9DOF Accel/Mag/Gyro+Temp: Add motion, direction and orientation sensing to your Arduino project with this all-in-one 9-DOF sensor. Inside the chip are three sensors, one is a classic 3-axis accelerometer, which can tell you which direction is down towards the Earth (by measuring gravity) or how fast the board is accelerating in 3D space. The other is a 3-axis magnetometer that can sense where the strongest magnetic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
