# Fritzing sketch Schéma moteur + gyro (saved by Fritzing 0.9.3b)
breadboards: 1

parts:
  M1 = DC Motor
  M3 = DC Motor
  M4 = DC Motor
  Composant2 = Adafruit DC+Stepper FeatherWing [part_number="Adafruit #2927"]
  M2 = DC Motor
  Composant3 = LSM9DS0 9DOF Accel/Mag/Gyro+Temp

nets:
  N1: M1.pin_1, Composant2.M2A
  N2: M1.pin_2, Composant2.M2B
  N3: M3.pin_1, Composant2.M4A
  N4: M3.pin_2, Composant2.M4B
  N5: M4.pin_1, Composant2.M3B
  N6: M4.pin_2, Composant2.M3A
  N7: Composant2.SCL, Composant3.SCL_5V
  N8: Composant2.SDA, Composant3.SDA_5V
  GND: Composant2.GND, Composant3.GND
  +3.3V: Composant2.+3.3V, Composant3.3V3
  N9: Composant2.M1B, M2.pin_1
  N10: Composant2.M1A, M2.pin_2

custom parts:
  Adafruit DC+Stepper FeatherWing: This is the DC Motor + Stepper FeatherWing which will let you use 2 x bi-polar stepper motors or 4 x brushed DC motorx (or 1 stepper and 2 DC motors). Using our Feather Stacking Headers or Feather Female Headers you can connect a FeatherWing on top or bottom of your Feather board and let the board take flight! The original Adafruit Motorshield Kit is one of our most beloved kits, which is why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
  LSM9DS0 9DOF Accel/Mag/Gyro+Temp: Add motion, direction and orientation sensing to your Arduino project with this all-in-one 9-DOF sensor. Inside the chip are three sensors, one is a classic 3-axis accelerometer, which can tell you which direction is down towards the Earth (by measuring gravity) or how fast the board is accelerating in 3D space. The other is a 3-axis magnetometer that can sense where the strongest magnetic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
