# Fritzing sketch Schéma receveur (saved by Fritzing 0.9.3b)
breadboards: 1

parts:
  Composant1 = Adafruit HUZZAH32 ESP32 Feather [part_number="Adafruit #3405"]
  NRF24L1 = NRF24L01

nets:
  N1: Composant1.MISO, NRF24L1.MISO
  N2: Composant1.SCK, NRF24L1.SCK
  GND: Composant1.GND, NRF24L1.GND
  3.3V: Composant1.3.3V, NRF24L1.VCC
  N3: Composant1.IO32_A7, NRF24L1.CSN
  N4: Composant1.IO14_A6, NRF24L1.CE

custom parts:
  NRF24L01: NRF24L01 module
