# Fritzing sketch Telecommande (saved by Fritzing 0.9.3b)
breadboards: 1

parts:
  Transceiver1 = nRF24L01 [package=module]
  Onderdeel3 = Thumb Joystick
  Onderdeel4 = Thumb Joystick
  Composant2 = Arduino Nano (Rev3.0)
  JP1 = Header 2 [package=jst-2-smd]  # not connected

nets:
  GND: Transceiver1.GND, Onderdeel3.GND, Onderdeel4.GND, Composant2.GND
  VCC: Transceiver1.VCC, Composant2.3V3
  N1: Transceiver1.CE, Composant2.A4
  N2: Transceiver1.CSN, Composant2.A5
  N3: Transceiver1.SCK, Composant2.D13/SCK
  N4: Transceiver1.MOSI, Composant2.D12/MISO
  N5: Transceiver1.MISO, Composant2.D11/MOSI
  N6: Onderdeel3.HORZ, Composant2.A2
  N7: Onderdeel3.VERT, Composant2.A3
  VCC_2: Onderdeel3.VCC, Onderdeel4.VCC, Composant2.5V
  N8: Onderdeel4.HORZ, Composant2.A0
  N9: Onderdeel4.VERT, Composant2.A1

custom parts:
  nRF24L01: nRF24L01 module
